# Fritzing sketch wiring (saved by Fritzing 0.9.3b)
breadboards: 1

parts:
  Part1 = Arduino Uno (Rev3) - ICSP
  Part2 = Mono 2.5W Class D Audio Amplifier - PAM8302
  VCC1 = Battery block 9V
  SP1 = SPEAKER [package=pcb_mount_speaker]

nets:
  N1: Part1.D7, Part2.AIN+
  GND: Part1.GND, Part2.GND, Part2.AIN-, VCC1.-
  N2: Part2.VCC, VCC1.+
  N3: Part2.VO+, SP1.+
  N4: Part2.VO-, SP1.-

custom parts:
  Mono 2.5W Class D Audio Amplifier - PAM8302: A super small but powerful mono amplifier able to deliver up to 2.5 Watts into 4-8 ohm impedance speakers. Inside the miniature chip is a class D controller, able to run from 2.0V-5.5VDC. Since the amp is a class D, its very efficient (over 90% efficient when driving an 8Ω speaker at over half a Watt) - making it perfect for portable and battery-powered projects.
