# Fritzing sketch robo-car1 (saved by Fritzing 0.9.3b)
breadboards: 1

parts:
  Part2 = Motor Driver 1A Dual TB6612FNG
  M1 = DC Motor
  M2 = DC Motor
  Part1 = Arduino Uno (Rev3)

nets:
  GND: Part2.GND, Part1.GND
  N1: Part2.B01, M2.pin_1
  N2: Part2.B02, M2.pin_2
  N3: Part2.A02, M1.pin_2
  N4: Part2.A01, M1.pin_1
  VCC: Part2.VCC, Part2.VM, Part1.5V
  N5: Part2.PWMA, Part1.D5_PWM
  N6: Part2.AIN2, Part1.D4
  N7: Part2.AIN1, Part1.D2
  N8: Part2.STBY, Part1.D9_PWM
  N9: Part2.BIN1, Part1.D7
  N10: Part2.BIN2, Part1.D8
  N11: Part2.PWMB, Part1.D6_PWM
