# Fritzing sketch multiple_values (saved by Fritzing 0.9.3b)
breadboards: 1

parts:
  Part1 = Arduino Uno (Rev3)
  R1 = Trimmer Potentiometer [maximum_resistance=10kΩ package=THT]
  R2 = Trimmer Potentiometer [maximum_resistance=10kΩ package=THT]
  S1 = Momentary Switch [package=ksa_sealed_tac_switch]
  R3 = Resistor [tolerance=±5% resistance=10k package="0805 [SMD]"]

nets:
  N1: Part1.A0, R1.wiper
  N2: Part1.A1, R2.wiper
  N3: Part1.D7, S1.1
  N4: Part1.5V, R1.leg1, R2.leg1, S1.4
  N5: Part1.GND, R1.leg2, R2.leg2, R3.Pin_1
  N6: S1.2, R3.Pin_0

notes:
  10k resistor
